// Logisim project 4 bit syn down counter.circ as structural Verilog: 1 circuit, main circuit main
module main (
  output out_1,
  output out_2,
  output out_3,
  output out_4
);

  wire clock_1_out, n7408_1_p3, n7408_1_p7, n7408_1_p8, n7476_1_p7, n7476_1_p11;

  Clock clock_1 (.out(clock_1_out));
  // _7476 7476_1: pin names not known; wires that end beside it: clock_1_out, 1'b1, 1'b1, clock_1_out, 1'b1, out_4, n7476_1_p7, 1'b0, n7476_1_p7, out_3, n7476_1_p11, n7476_1_p7
  // _7408 7408_1: pin names not known; wires that end beside it: n7476_1_p7, n7476_1_p11, n7408_1_p3, 1'b0, 1'b1, n7408_1_p3, n7408_1_p7, n7408_1_p8
  // _7476 7476_2: pin names not known; wires that end beside it: clock_1_out, n7408_1_p3, 1'b1, clock_1_out, n7408_1_p3, out_2, n7408_1_p7, 1'b0, n7408_1_p8, out_1, n7408_1_p8
endmodule
