// Logisim project Johnson counter.circ as structural Verilog: 1 circuit, main circuit main
module main (
  output Q0,
  output Q1,
  output Q2,
  output Q3
);

  wire clock_1_out, INIT_out, n7474_1_p2;

  Button INIT (.out(INIT_out));
  Clock clock_1 (.out(clock_1_out));
  // _7474 7474_1: pin names not known; wires that end beside it: INIT_out, n7474_1_p2, clock_1_out, Q0, 1'b0, 1'b1, INIT_out, Q0, clock_1_out, Q1
  // _7474 7474_2: pin names not known; wires that end beside it: INIT_out, Q1, clock_1_out, Q2, 1'b0, 1'b1, INIT_out, Q2, clock_1_out, Q3, n7474_1_p2

  // Notes on the sheet:
  //   4BIT JOHNSON COUNTER
endmodule
