// Logisim project 4 bit ripple up counter.circ as structural Verilog: 1 circuit, main circuit main
module main (
  output out_1,
  output out_2,
  output out_3,
  output out_4
);

  wire Initialize_out, n7476_1_p1, n7476_1_p4, n7476_2_p1, n7476_2_p4;

  Button Initialize (.out(Initialize_out));
  // _7476 7476_1: pin names not known; wires that end beside it: n7476_1_p1, Initialize_out, 1'b1, n7476_1_p4, Initialize_out, 1'b1, out_1, 1'b1, out_2, n7476_1_p1, 1'b1
  // _7476 7476_2: pin names not known; wires that end beside it: n7476_2_p1, Initialize_out, 1'b1, n7476_2_p4, Initialize_out, 1'b1, out_3, n7476_1_p4, 1'b1, out_4, n7476_2_p1, 1'b1
  Clock clock_1 (.out(n7476_2_p4));

  // Notes on the sheet:
  //   4 bit ripple up counter
endmodule
