// Logisim project 4-bit-syn-up-counter.circ as structural Verilog: 1 circuit, main circuit main
module main (
  output out_1,
  output out_2,
  output out_3,
  output out_4
);

  wire clock_1_out, n7404_1_p2, n7408_2_p4, n7408_2_p7, n7476_1_p2, n7476_2_p3, n7476_2_p10;

  Clock clock_1 (.out(clock_1_out));
  // _7476 7476_1: pin names not known; wires that end beside it: clock_1_out, n7476_1_p2, 1'b1, 1'b1, clock_1_out, n7476_1_p2, 1'b1, out_4, 1'b0, out_4, out_3, out_4
  // _7476 7476_2: pin names not known; wires that end beside it: clock_1_out, n7476_1_p2, n7476_2_p3, 1'b1, clock_1_out, n7476_1_p2, n7476_2_p3, out_2, 1'b0, n7476_2_p10, out_1, n7476_2_p10, 1'b0
  // _7408 7408_1: pin names not known; wires that end beside it: out_4, out_3, n7476_2_p3, n7476_2_p3, out_2, n7476_2_p10, 1'b1
  // _7404 7404_1: pin names not known; wires that end beside it: out_3, n7404_1_p2, 1'b1
  // _7408 7408_2: pin names not known; wires that end beside it: 1'b0, out_1, out_2, n7408_2_p4, n7408_2_p4, n7404_1_p2, n7408_2_p7, 1'b0, 1'b1, n7408_2_p7, out_4, n7476_1_p2

  // Notes on the sheet:
  //   mod 12 counter
endmodule
