// Logisim project binary_counter.circ as structural Verilog: 1 circuit, main circuit main
module main (
  output out_1,
  output out_2,
  output out_3,
  output out_4,
  output out_5,
  output out_6
);

  wire and_1_out, and_2_out, and_3_out, and_4_out, and_5_out, and_6_out, and_7_out, and_8_out, clock_1_out,
       s_r_ff_1_qn, s_r_ff_2_qn, s_r_ff_3_qn, s_r_ff_4_qn, s_r_ff_5_qn, s_r_ff_6_qn;

  Clock clock_1 (.out(clock_1_out));
  and and_1 (and_1_out, s_r_ff_1_qn, and_6_out);
  and and_2 (and_2_out, out_1, and_6_out);
  and and_3 (and_3_out, s_r_ff_2_qn, and_8_out);
  and and_4 (and_4_out, out_4, and_8_out);
  and and_5 (and_5_out, s_r_ff_3_qn, out_3);
  S_R_Flip_Flop s_r_ff_1 (
    .S(and_1_out), .clk(s_r_ff_2_qn), .R(and_2_out), .Q(out_1), .Qn(s_r_ff_1_qn), .en(1'b1));  // open: preset, reset
  and and_6 (and_6_out, out_2, out_3);
  and and_7 (and_7_out, s_r_ff_4_qn, out_6);
  S_R_Flip_Flop s_r_ff_2 (
    .S(and_3_out), .clk(clock_1_out), .R(and_4_out), .Q(out_4), .Qn(s_r_ff_2_qn), .en(1'b1));  // open: preset, reset
  S_R_Flip_Flop s_r_ff_3 (
    .S(and_5_out), .clk(s_r_ff_2_qn), .R(and_6_out), .Q(out_2), .Qn(s_r_ff_3_qn), .en(1'b1));  // open: preset, reset
  S_R_Flip_Flop s_r_ff_4 (
    .S(and_7_out), .clk(clock_1_out), .R(and_8_out), .Q(out_5), .Qn(s_r_ff_4_qn), .en(1'b1));  // open: preset, reset
  and and_8 (and_8_out, out_5, out_6);
  S_R_Flip_Flop s_r_ff_5 (
    .S(s_r_ff_5_qn), .clk(s_r_ff_2_qn), .R(out_3), .Q(out_3), .Qn(s_r_ff_5_qn), .en(1'b1));  // open: preset, reset
  S_R_Flip_Flop s_r_ff_6 (
    .S(s_r_ff_6_qn), .clk(clock_1_out), .R(out_6), .Q(out_6), .Qn(s_r_ff_6_qn), .en(1'b1));  // open: preset, reset
endmodule
