// Logisim project modulo-8-counter.circ as structural Verilog: 1 circuit, main circuit main
module main (
  output out_1,
  output out_2,
  output out_3,
  output Z
);

  wire clock_1_out, n7408_1_p6, n7476_1_p6;

  Clock clock_1 (.out(clock_1_out));
  // _7476 7476_1: pin names not known; wires that end beside it: clock_1_out, 1'b1, clock_1_out, 1'b1, out_3, n7476_1_p6, out_2, n7476_1_p6
  // _7408 7408_1: pin names not known; wires that end beside it: 1'b1, out_3, n7476_1_p6, out_2, n7476_1_p6, n7408_1_p6, n7408_1_p6, out_1, Z
  // _7476 7476_2: pin names not known; wires that end beside it: clock_1_out, n7408_1_p6, clock_1_out, n7408_1_p6, out_1
endmodule
